# Fritzing sketch ActivityIndicatorFritzing (saved by Fritzing 0.9.9b)

parts:
  LED1 = smd LED [color="Red (633nm)" package="0603 [SMD]"]
  R1 = Resistor [tolerance=±5% power=0.25 resistance=1000 package=THT]
  LED2 = DUO LED RG [package="5 mm [THT]"]
  R2 = Resistor [tolerance=±5% power=0.25 resistance=1000 package=THT]
  MCU1 = Raspberry Pi Zero
  S1 = Taiway 100-SP-X-T1 SPDT Miniature Toggle Switch [part_number=100-SP-X-T1-0-0-B1-M2 package=THT]

nets:
  N1: LED1.cathode, R2.Pin_0, MCU1.pin_6, MCU1.pin_20, MCU1.pin_30, MCU1.pin_34, MCU1.pin_39, S1.COM
  N2: LED1.anode, R1.Pin_0
  N3: R1.Pin_1, MCU1.pin_2, MCU1.pin_4
  N4: LED2.red_anode, MCU1.pin_38
  N5: LED2.common_cathode, R2.Pin_1
  N6: LED2.green_anode, MCU1.pin_40
  N7: MCU1.pin_36, S1.L1

notes:
  Green
  Red
  100 Ohm
  1k Ohm
  Connection indicator
  Power indicator
  Open
  Closed
  Pins:
  Power LED - 5V
  Switch - GPIO 16
  ConLED Green - GPIO 20
  ConLED Red - GPIO 21
